// Logisim project new_arc.circ as structural Verilog: 12 circuits, main circuit main
module main (
  input  reset,
  output [12:0] out_2,
  output [7:0] out_3,
  output [7:0] out_4,
  output [7:0] out_5,
  output [7:0] out_6,
  output [7:0] out_7
);

  wire clock_1_out, not_1_out, not_2_out;
  wire [1:0] alu_and_regesters_1_out_8;
  wire [6:0] instruction_reg_1_out_6;
  wire [7:0] alu_and_regesters_1_out_6, display_driver_1_out_5, display_driver_1_out_6,
       display_driver_1_out_7, display_driver_1_out_8, display_driver_1_out_9, display_driver_1_out_10,
       display_driver_1_out_11, display_driver_1_out_12, display_driver_1_out_13, display_driver_1_out_14,
       display_driver_1_out_15, display_driver_1_out_16, display_driver_1_out_17, display_driver_1_out_18,
       display_driver_1_out_19, display_driver_1_out_20, display_driver_1_out_21, display_driver_1_out_22,
       display_driver_1_out_23, display_driver_1_out_24, display_driver_1_out_25, display_driver_1_out_26,
       display_driver_1_out_27, display_driver_1_out_28, display_driver_1_out_29, display_driver_1_out_30,
       display_driver_1_out_31, display_driver_1_out_32, display_driver_1_out_33, display_driver_1_out_34,
       display_driver_1_out_35, display_driver_1_out_36, input_output_1_out_5, input_output_1_out_6,
       multiplexer_1_out, stack_pointer_1_out_5;
  wire [8:0] instruction_reg_1_out_7;
  wire [10:0] instruction_reg_1_out_8;

  Clock clock_1 (.out(clock_1_out));
  instruction_reg instruction_reg_1 (
    .clk(out_6), .in_2(clock_1_out), .out_6(instruction_reg_1_out_6), .out_7(instruction_reg_1_out_7),
    .out_8(instruction_reg_1_out_8), .Flag_register(alu_and_regesters_1_out_8), .out_5(out_2), .in_4(reset));
  not not_1 (not_1_out, instruction_reg_1_out_8[9]);
  stack_pointer stack_pointer_1 (
    .in_1(instruction_reg_1_out_8[8]), .sp_sel(instruction_reg_1_out_8[7]), .in_3(clock_1_out),
    .out_5(stack_pointer_1_out_5), .in_4(reset));
  _8bit_counter u_8bit_counter_1 (
    .in_2(out_6), .out_8(out_7), .in_4(clock_1_out), .in_3(instruction_reg_1_out_8[2]),
    .in_1(instruction_reg_1_out_8[3]), .in_5(instruction_reg_1_out_8[10]), .out_7(out_6), .in_6(reset));
  Multiplexer #(.select(2), .width(8), .enable("false")) multiplexer_1 (
    .in0(stack_pointer_1_out_5), .in1(alu_and_regesters_1_out_6), .in2(out_5), .in3(out_7),
    .out(multiplexer_1_out), .sel(instruction_reg_1_out_8[1:0]));
  alu_and_regesters alu_and_regesters_1 (
    .in_1(instruction_reg_1_out_6), .in_2(instruction_reg_1_out_7), .in_4(clock_1_out), .out_7(out_3),
    .out_9(out_4), .out_10(out_5), .in_3(out_6), .out_6(alu_and_regesters_1_out_6),
    .out_8(alu_and_regesters_1_out_8), .in_5(instruction_reg_1_out_8[6]), .out_11(out_6));
  not not_2 (not_2_out, clock_1_out);
  RAM #(.bus("separate")) ram_1 (
    .addr(multiplexer_1_out), .din(out_6), .data(out_6), .str(instruction_reg_1_out_8[5]), .sel(not_1_out),
    .clk(not_2_out), .ld(instruction_reg_1_out_8[4]));  // open: clr
  // Probe on out_3
  INPUT_OUTPUT input_output_1 (
    .in_1(out_6), .in_2(multiplexer_1_out), .CLK(clock_1_out), .I_O_ENABLE(instruction_reg_1_out_8[9]),
    .out_5(input_output_1_out_5), .out_6(input_output_1_out_6));
  DotMatrix #(.matrixcols(32), .matrixrows(8)) dotmatrix_1 (
    .col0(display_driver_1_out_5), .col1(display_driver_1_out_6), .col2(display_driver_1_out_7),
    .col3(display_driver_1_out_8), .col4(display_driver_1_out_9), .col5(display_driver_1_out_10),
    .col6(display_driver_1_out_11), .col7(display_driver_1_out_12), .col8(display_driver_1_out_13),
    .col9(display_driver_1_out_14), .col10(display_driver_1_out_15), .col11(display_driver_1_out_16),
    .col12(display_driver_1_out_17), .col13(display_driver_1_out_18), .col14(display_driver_1_out_19),
    .col15(display_driver_1_out_20), .col16(display_driver_1_out_21), .col17(display_driver_1_out_22),
    .col18(display_driver_1_out_23), .col19(display_driver_1_out_24), .col20(display_driver_1_out_25),
    .col21(display_driver_1_out_26), .col22(display_driver_1_out_27), .col23(display_driver_1_out_28),
    .col24(display_driver_1_out_29), .col25(display_driver_1_out_30), .col26(display_driver_1_out_31),
    .col27(display_driver_1_out_32), .col28(display_driver_1_out_33), .col29(display_driver_1_out_34),
    .col30(display_driver_1_out_35), .col31(display_driver_1_out_36));
  display_driver display_driver_1 (
    .in_1(input_output_1_out_5), .in_2(input_output_1_out_6[0]), .in_3(input_output_1_out_6[1]),
    .out_5(display_driver_1_out_5), .out_6(display_driver_1_out_6), .out_7(display_driver_1_out_7),
    .out_8(display_driver_1_out_8), .out_9(display_driver_1_out_9), .out_10(display_driver_1_out_10),
    .out_11(display_driver_1_out_11), .out_12(display_driver_1_out_12), .out_13(display_driver_1_out_13),
    .out_14(display_driver_1_out_14), .out_15(display_driver_1_out_15), .out_16(display_driver_1_out_16),
    .out_17(display_driver_1_out_17), .out_18(display_driver_1_out_18), .out_19(display_driver_1_out_19),
    .out_20(display_driver_1_out_20), .out_21(display_driver_1_out_21), .out_22(display_driver_1_out_22),
    .out_23(display_driver_1_out_23), .out_24(display_driver_1_out_24), .out_25(display_driver_1_out_25),
    .out_26(display_driver_1_out_26), .out_27(display_driver_1_out_27), .out_28(display_driver_1_out_28),
    .out_29(display_driver_1_out_29), .out_30(display_driver_1_out_30), .out_31(display_driver_1_out_31),
    .out_32(display_driver_1_out_32), .out_33(display_driver_1_out_33), .out_34(display_driver_1_out_34),
    .out_35(display_driver_1_out_35), .out_36(display_driver_1_out_36), .in_4(reset));

  // Notes on the sheet:
  //   INPUT/OUPUT
endmodule

module _8bit_reg (
  input  [7:0] in_1,
  input  [7:0] in_2,
  input  clk,
  input  select,
  input  out_enable,
  input  _0___data_bus,
  output [7:0] out_7,
  output [7:0] out_8
);

  wire and_1_out;
  wire [7:0] multiplexer_1_out;

  and and_1 (and_1_out, clk, select);
  Multiplexer #(.width(8), .enable("false")) multiplexer_1 (
    .in0(in_1), .in1(in_2), .out(multiplexer_1_out), .sel(_0___data_bus));
  D_Flip_Flop #(.trigger("falling")) d_ff_1 (
    .clk(and_1_out), .D(multiplexer_1_out[0]), .Q(out_7[0]));  // open: Qn, preset, en, reset
  D_Flip_Flop #(.trigger("falling")) d_ff_2 (
    .clk(and_1_out), .D(multiplexer_1_out[1]), .Q(out_7[1]));  // open: Qn, preset, en, reset
  D_Flip_Flop #(.trigger("falling")) d_ff_3 (
    .clk(and_1_out), .D(multiplexer_1_out[2]), .Q(out_7[2]));  // open: Qn, preset, en, reset
  D_Flip_Flop #(.trigger("falling")) d_ff_4 (
    .clk(and_1_out), .D(multiplexer_1_out[3]), .Q(out_7[3]));  // open: Qn, preset, en, reset
  D_Flip_Flop #(.trigger("falling")) d_ff_5 (
    .clk(and_1_out), .D(multiplexer_1_out[4]), .Q(out_7[4]));  // open: Qn, preset, en, reset
  D_Flip_Flop #(.trigger("falling")) d_ff_6 (
    .clk(and_1_out), .D(multiplexer_1_out[5]), .Q(out_7[5]));  // open: Qn, preset, en, reset
  D_Flip_Flop #(.trigger("falling")) d_ff_7 (
    .clk(and_1_out), .D(multiplexer_1_out[6]), .Q(out_7[6]));  // open: Qn, preset, en, reset
  D_Flip_Flop #(.trigger("falling")) d_ff_8 (
    .clk(and_1_out), .D(multiplexer_1_out[7]), .Q(out_7[7]));  // open: Qn, preset, en, reset
  assign out_8 = out_enable ? out_7 : 8'bz;  // Controlled_Buffer controlled_buffer_1

  // Notes on the sheet:
  //   data bus
  //   alu
  //   1 -> ALU
endmodule

module ALU (
  input  [7:0] in_1,
  input  [6:0] in_2,
  input  [7:0] in_3,
  input  in_4,
  output [7:0] out_5,
  output [7:0] out_6,
  output [1:0] out_7
);

  wire adder_1_cout, and_1_out, nor_1_out, not_1_out, not_2_out, not_3_out, not_4_out, not_5_out, not_6_out,
       not_7_out, not_8_out, not_9_out, not_10_out, not_11_out, not_12_out;
  wire [7:0] adder_1_out, and_2_out, controled_inv_1_out_3, controled_inv_2_out_3, multiplexer_1_out,
       multiplexer_2_out, multiplexer_3_out;

  not not_1 (not_1_out, in_4);
  not not_2 (not_2_out, not_3_out);
  not not_3 (not_3_out, not_1_out);
  not not_4 (not_4_out, not_5_out);
  not not_5 (not_5_out, not_2_out);
  not not_6 (not_6_out, not_4_out);
  Pull_Resistor pull_resistor_1 (.node(in_3));
  not not_7 (not_7_out, not_9_out);
  not not_8 (not_8_out, not_7_out);
  not not_9 (not_9_out, not_6_out);
  controled_inv controled_inv_1 (.in_1(multiplexer_1_out), .in_2(in_2[1]), .out_3(controled_inv_1_out_3));
  Multiplexer #(.width(8), .enable("false")) multiplexer_1 (
    .in0(in_1), .in1({8{1'b0}}), .out(multiplexer_1_out), .sel(in_2[0]));
  Multiplexer #(.width(8), .enable("false")) multiplexer_2 (
    .in0(in_3), .in1({8{1'b0}}), .out(multiplexer_2_out), .sel(in_2[2]));
  controled_inv controled_inv_2 (.in_1(multiplexer_2_out), .in_2(in_2[3]), .out_3(controled_inv_2_out_3));
  not not_10 (not_10_out, not_11_out);
  not not_11 (not_11_out, not_8_out);
  and and_1 (and_1_out, in_4, not_12_out);
  not not_12 (not_12_out, not_10_out);
  Adder adder_1 (
    .a(controled_inv_1_out_3), .b(controled_inv_2_out_3), .out(adder_1_out), .cout(adder_1_cout));  // open: cin
  assign and_2_out = controled_inv_1_out_3 & controled_inv_2_out_3;  // AND_Gate and_2, 8 bits wide
  Multiplexer #(.width(8), .enable("false")) multiplexer_3 (
    .in0(adder_1_out), .in1(and_2_out), .out(multiplexer_3_out), .sel(in_2[5]));
  controled_inv controled_inv_3 (.in_1(multiplexer_3_out), .in_2(in_2[4]), .out_3(out_5));
  assign out_6 = in_2[6] ? out_5 : 8'bz;  // Controlled_Buffer controlled_buffer_1
  nor nor_1 (nor_1_out, out_5[0], out_5[1], out_5[2], out_5[3], out_5[4], out_5[5], out_5[6], out_5[7]);
  D_Flip_Flop #(.trigger("falling")) d_ff_1 (
    .clk(and_1_out), .D(nor_1_out), .Q(out_7[0]));  // open: Qn, preset, en, reset
  D_Flip_Flop #(.trigger("falling")) d_ff_2 (
    .clk(and_1_out), .D(adder_1_cout), .Q(out_7[1]));  // open: Qn, preset, en, reset

  // Notes on the sheet:
  //   X
  //   Z x
  //   INV X
  //   Y
  //   Z y
  //   INV Y
  //   INV out
  //   X+Y||X&Y
  //   0           1
endmodule

module controled_inv (
  input  [7:0] in_1,
  input  in_2,
  output [7:0] out_3
);

  xor xor_1 (out_3[0], in_1[0], in_2);
  xor xor_2 (out_3[1], in_1[1], in_2);
  xor xor_3 (out_3[2], in_1[2], in_2);
  xor xor_4 (out_3[3], in_1[3], in_2);
  xor xor_5 (out_3[4], in_1[4], in_2);
  xor xor_6 (out_3[5], in_1[5], in_2);
  xor xor_7 (out_3[6], in_1[6], in_2);
  xor xor_8 (out_3[7], in_1[7], in_2);
endmodule

module _8bit_counter (
  input  in_1,
  input  [7:0] in_2,
  input  in_3,
  input  in_4,
  input  in_5,
  input  in_6,
  output [7:0] out_7,
  output [7:0] out_8
);

  wire and_1_out, and_2_out;

  and and_1 (and_1_out, in_1, in_3);
  Counter #(.ongoal("continue"), .trigger("falling")) counter_1 (
    .load(and_1_out), .D(in_2), .count(and_2_out), .Q(out_8), .clk(in_4), .clr(in_6));  // open: carry
  and and_2 (and_2_out, ~in_1, in_3);  // AND_Gate
  assign out_7 = in_5 ? out_8 : 8'bz;  // Controlled_Buffer controlled_buffer_1
endmodule

module _3bit_counter (
  input  in_1,
  input  in_2,
  input  in_3,
  output out_4,
  output out_5,
  output out_6
);

  wire d_ff_1_q, d_ff_2_qn, d_ff_3_qn, d_ff_4_qn, multiplexer_1_out, not_1_out;

  D_Flip_Flop #(.trigger("falling")) d_ff_1 (
    .clk(in_1), .D(in_2), .Q(d_ff_1_q), .reset(not_1_out));  // open: Qn, preset, en
  not not_1 (not_1_out, in_2);
  Multiplexer #(.enable("false")) multiplexer_1 (.in0(d_ff_1_q), .in1(1'b1), .out(multiplexer_1_out), .sel(in_3));
  D_Flip_Flop #(.trigger("falling")) d_ff_2 (
    .clk(in_1), .D(d_ff_2_qn), .Q(out_4), .Qn(d_ff_2_qn), .reset(multiplexer_1_out));  // open: preset, en
  D_Flip_Flop #(.trigger("falling")) d_ff_3 (
    .clk(out_4), .D(d_ff_3_qn), .Q(out_5), .Qn(d_ff_3_qn), .reset(multiplexer_1_out));  // open: preset, en
  D_Flip_Flop #(.trigger("falling")) d_ff_4 (
    .clk(out_5), .D(d_ff_4_qn), .Q(out_6), .Qn(d_ff_4_qn), .reset(multiplexer_1_out));  // open: preset, en
endmodule

module instruction_reg (
  input  [7:0] clk,
  input  in_2,
  input  [1:0] Flag_register,
  input  in_4,
  output [12:0] out_5,
  output [6:0] out_6,
  output [8:0] out_7,
  output [10:0] out_8
);

  wire and_1_out, nor_1_out, not_1_out, not_2_out, not_3_out, not_4_out, not_5_out, not_6_out, not_7_out,
       not_8_out, not_9_out, not_10_out, not_11_out, not_12_out;
  wire [23:23] rom_1_data;

  _3bit_counter u_3bit_counter_1 (
    .in_1(in_2), .out_4(out_5[10]), .out_5(out_5[11]), .in_2(rom_1_data[23]), .out_6(out_5[12]), .in_3(in_4));
  nor nor_1 (nor_1_out, out_5[10], out_5[11], out_5[12]);
  not not_1 (not_1_out, not_3_out);
  not not_2 (not_2_out, not_1_out);
  not not_3 (not_3_out, nor_1_out);
  not not_4 (not_4_out, not_2_out);
  not not_5 (not_5_out, not_4_out);
  _8bit_reg u_8bit_reg_1 (
    .clk(and_1_out), .select(and_1_out), .out_7(out_5[9:2]), .in_1(clk), ._0___data_bus(1'b0));  // open: out_8, out_enable, in_2
  not not_6 (not_6_out, not_5_out);
  not not_7 (not_7_out, not_8_out);
  not not_8 (not_8_out, not_6_out);
  not not_9 (not_9_out, not_10_out);
  not not_10 (not_10_out, not_7_out);
  not not_11 (not_11_out, not_9_out);
  and and_1 (and_1_out, nor_1_out, not_12_out);
  not not_12 (not_12_out, not_11_out);
  ROM #(.addrWidth(13), .dataWidth(28)) rom_1 (
    .addr({out_5[12:2], Flag_register}),
    .data({out_7[8:7], out_8[10:9], rom_1_data[23], out_8[8:0], out_7[6:0], out_6}), .sel(1'b1));

  assign out_5[1:0] = Flag_register;

  // Notes on the sheet:
  //   data bus
  //   contents of rom_1 (hex, n*v repeats v):
  //   1024*5c000 4*85c080 4*85c400 4*85d000 4*90ca80 4*90ca92 4*90e280 4*90e292 4*80c000 4*87c000 81c000
  //   87c000 81c000 87c000 81c000 81c000 87c000 87c000 4*4c080 4*4d000 4*90c29e 4*90c28c 4*95c280 4*90caa0
  //   4*95c2a0 4*4c080 4*4d000 4*490cc1b 4*490cc03 4*200d000 4*60c000 4*a80100 4*840080 4*a80100 4*840400
  //   4*90d812 4*95d012 87c000 81c000 87c000 81c000 87c000 87c000 81c000 81c000 940*0 4*854084 4*898100
  //   20*0 4*ca80 4*1818100 8*0 4*800f01b 4*870000 1000*0 4*854084 12*0 4*282000 1020*0 4*87c000
  //   ALU controll
  //   Ram IP SP controll
  //   Register controll
endmodule

module alu_and_regesters (
  input  [6:0] in_1,
  input  [8:0] in_2,
  input  [7:0] in_3,
  input  in_4,
  input  in_5,
  output [7:0] out_6,
  output [7:0] out_7,
  output [1:0] out_8,
  output [7:0] out_9,
  output [7:0] out_10,
  output [7:0] out_11
);

  wire and_1_out, and_2_out, or_1_out, or_2_out;
  wire [7:0] n8bit_reg_1_out_8;

  or or_1 (or_1_out, in_2[1], in_2[4], in_2[6]);
  or or_2 (or_2_out, in_2[0], in_2[3], in_2[5]);
  _8bit_reg u_8bit_reg_1 (
    .clk(in_4), .select(in_2[0]), .out_8(n8bit_reg_1_out_8), .out_enable(in_2[1]), .out_7(out_7),
    .in_1(n8bit_reg_1_out_8), .in_2(out_6), ._0___data_bus(in_2[2]));
  _8bit_reg u_8bit_reg_2 (
    .clk(in_4), .select(in_2[3]), .out_8(n8bit_reg_1_out_8), .out_enable(in_2[4]), .out_7(out_9),
    .in_1(n8bit_reg_1_out_8), .in_2(out_6), ._0___data_bus(in_2[7]));
  _8bit_reg u_8bit_reg_3 (
    .clk(in_4), .select(in_2[5]), .out_8(n8bit_reg_1_out_8), .out_enable(in_2[6]), .out_7(out_10),
    .in_1(n8bit_reg_1_out_8), .in_2(out_6), ._0___data_bus(in_2[8]));
  and and_1 (and_1_out, or_1_out, ~or_2_out);  // AND_Gate
  and and_2 (and_2_out, ~or_1_out, or_2_out);  // AND_Gate
  ALU alu_1 (
    .in_1(out_7), .in_3(n8bit_reg_1_out_8), .out_6(n8bit_reg_1_out_8), .in_2(in_1), .out_5(out_6),
    .in_4(in_5), .out_7(out_8));
  assign n8bit_reg_1_out_8 = and_2_out ? in_3 : 8'bz;  // Controlled_Buffer controlled_buffer_1
  assign out_11 = and_1_out ? n8bit_reg_1_out_8 : 8'bz;  // Controlled_Buffer controlled_buffer_2

  // Notes on the sheet:
  //   out
  //   in
endmodule

module _8bit27seg (
  input  [7:0] in_1,
  output [3:0] out_2,
  output [3:0] out_3
);

  Hex_Digit_Display hex_digit_display_1 (.value(in_1[7:4]));  // open: dp
  Hex_Digit_Display hex_digit_display_2 (.value(in_1[3:0]));  // open: dp

  assign out_2 = in_1[3:0];
  assign out_3 = in_1[7:4];
endmodule

module INPUT_OUTPUT (
  input  [7:0] in_1,
  input  [7:0] in_2,
  input  CLK,
  input  I_O_ENABLE,
  output [7:0] out_5,
  output [7:0] out_6
);

  wire and_1_out, and_2_out;

  and and_1 (and_1_out, ~in_2[0], ~in_2[1], ~in_2[2], ~in_2[3], ~in_2[4], ~in_2[5], ~in_2[6], ~in_2[7], I_O_ENABLE);  // AND_Gate
  and and_2 (and_2_out, in_2[0], ~in_2[1], ~in_2[2], ~in_2[3], ~in_2[4], ~in_2[5], ~in_2[6], ~in_2[7], I_O_ENABLE);  // AND_Gate
  _8bit_reg u_8bit_reg_1 (
    .clk(CLK), .select(and_1_out), .out_7(out_5), .in_1(in_1), ._0___data_bus(1'b0));  // open: out_8, out_enable, in_2
  _8bit_reg u_8bit_reg_2 (
    .clk(CLK), .select(and_2_out), .out_7(out_6), .in_1(in_1), ._0___data_bus(1'b0));  // open: out_8, out_enable, in_2

  // Notes on the sheet:
  //   ADRESS BUS
  //   PORTA
  //   PORTB
endmodule

module display_driver (
  input  [7:0] in_1,
  input  in_2,
  input  in_3,
  input  in_4,
  output [7:0] out_5,
  output [7:0] out_6,
  output [7:0] out_7,
  output [7:0] out_8,
  output [7:0] out_9,
  output [7:0] out_10,
  output [7:0] out_11,
  output [7:0] out_12,
  output [7:0] out_13,
  output [7:0] out_14,
  output [7:0] out_15,
  output [7:0] out_16,
  output [7:0] out_17,
  output [7:0] out_18,
  output [7:0] out_19,
  output [7:0] out_20,
  output [7:0] out_21,
  output [7:0] out_22,
  output [7:0] out_23,
  output [7:0] out_24,
  output [7:0] out_25,
  output [7:0] out_26,
  output [7:0] out_27,
  output [7:0] out_28,
  output [7:0] out_29,
  output [7:0] out_30,
  output [7:0] out_31,
  output [7:0] out_32,
  output [7:0] out_33,
  output [7:0] out_34,
  output [7:0] out_35,
  output [7:0] out_36
);

  wire [7:0] shift_register_1_q0, shift_register_1_q1, shift_register_1_q2, shift_register_1_q3,
       shift_register_1_q4, shift_register_1_q5, shift_register_1_q6, shift_register_1_q7,
       shift_register_1_q8, shift_register_1_q9, shift_register_1_q10, shift_register_1_q11,
       shift_register_1_q12, shift_register_1_q13, shift_register_1_q14, shift_register_1_q15,
       shift_register_1_q16, shift_register_1_q17, shift_register_1_q18, shift_register_1_q19,
       shift_register_1_q20, shift_register_1_q21, shift_register_1_q22, shift_register_1_q23,
       shift_register_1_q24, shift_register_1_q25, shift_register_1_q26, shift_register_1_q27,
       shift_register_1_q28, shift_register_1_q29, shift_register_1_q30, shift_register_1_q31;

  Shift_Register #(.width(8), .length(32), .trigger("falling")) shift_register_1 (
    .shift(1'b1), .in(in_1), .clk(in_2), .clr(in_4), .q0(shift_register_1_q0), .q1(shift_register_1_q1),
    .q2(shift_register_1_q2), .q3(shift_register_1_q3), .q4(shift_register_1_q4), .q5(shift_register_1_q5),
    .q6(shift_register_1_q6), .q7(shift_register_1_q7), .q8(shift_register_1_q8), .q9(shift_register_1_q9),
    .q10(shift_register_1_q10), .q11(shift_register_1_q11), .q12(shift_register_1_q12),
    .q13(shift_register_1_q13), .q14(shift_register_1_q14), .q15(shift_register_1_q15),
    .q16(shift_register_1_q16), .q17(shift_register_1_q17), .q18(shift_register_1_q18),
    .q19(shift_register_1_q19), .q20(shift_register_1_q20), .q21(shift_register_1_q21),
    .q22(shift_register_1_q22), .q23(shift_register_1_q23), .q24(shift_register_1_q24),
    .q25(shift_register_1_q25), .q26(shift_register_1_q26), .q27(shift_register_1_q27),
    .q28(shift_register_1_q28), .q29(shift_register_1_q29), .q30(shift_register_1_q30),
    .q31(shift_register_1_q31));  // open: out, load, d0, d1, d2, d3, d4, d5, d6, d7, d8, d9, d10, d11, d12, d13, d14, d15, d16, d17, d18, d19, d20, d21, d22, d23, d24, d25, d26, d27, d28, d29, d30, d31
  Register #(.trigger("falling")) register_1 (.D(shift_register_1_q0), .Q(out_5), .clk(in_3), .clr(in_4));  // open: en
  Register #(.trigger("falling")) register_2 (.D(shift_register_1_q1), .Q(out_6), .clk(in_3), .clr(in_4));  // open: en
  Register #(.trigger("falling")) register_3 (.D(shift_register_1_q2), .Q(out_7), .clk(in_3), .clr(in_4));  // open: en
  Register #(.trigger("falling")) register_4 (.D(shift_register_1_q3), .Q(out_8), .clk(in_3), .clr(in_4));  // open: en
  Register #(.trigger("falling")) register_5 (.D(shift_register_1_q4), .Q(out_9), .clk(in_3), .clr(in_4));  // open: en
  Register #(.trigger("falling")) register_6 (.D(shift_register_1_q5), .Q(out_10), .clk(in_3), .clr(in_4));  // open: en
  Register #(.trigger("falling")) register_7 (.D(shift_register_1_q6), .Q(out_11), .clk(in_3), .clr(in_4));  // open: en
  Register #(.trigger("falling")) register_8 (.D(shift_register_1_q7), .Q(out_12), .clk(in_3), .clr(in_4));  // open: en
  Register #(.trigger("falling")) register_9 (.D(shift_register_1_q8), .Q(out_13), .clk(in_3), .clr(in_4));  // open: en
  Register #(.trigger("falling")) register_10 (
    .D(shift_register_1_q9), .Q(out_14), .clk(in_3), .clr(in_4));  // open: en
  Register #(.trigger("falling")) register_11 (
    .D(shift_register_1_q10), .Q(out_15), .clk(in_3), .clr(in_4));  // open: en
  Register #(.trigger("falling")) register_12 (
    .D(shift_register_1_q11), .Q(out_16), .clk(in_3), .clr(in_4));  // open: en
  Register #(.trigger("falling")) register_13 (
    .D(shift_register_1_q12), .Q(out_17), .clk(in_3), .clr(in_4));  // open: en
  Register #(.trigger("falling")) register_14 (
    .D(shift_register_1_q13), .Q(out_18), .clk(in_3), .clr(in_4));  // open: en
  Register #(.trigger("falling")) register_15 (
    .D(shift_register_1_q14), .Q(out_19), .clk(in_3), .clr(in_4));  // open: en
  Register #(.trigger("falling")) register_16 (
    .D(shift_register_1_q15), .Q(out_20), .clk(in_3), .clr(in_4));  // open: en
  Register #(.trigger("falling")) register_17 (
    .D(shift_register_1_q16), .Q(out_21), .clk(in_3), .clr(in_4));  // open: en
  Register #(.trigger("falling")) register_18 (
    .D(shift_register_1_q17), .Q(out_22), .clk(in_3), .clr(in_4));  // open: en
  Register #(.trigger("falling")) register_19 (
    .D(shift_register_1_q18), .Q(out_23), .clk(in_3), .clr(in_4));  // open: en
  Register #(.trigger("falling")) register_20 (
    .D(shift_register_1_q19), .Q(out_24), .clk(in_3), .clr(in_4));  // open: en
  Register #(.trigger("falling")) register_21 (
    .D(shift_register_1_q20), .Q(out_25), .clk(in_3), .clr(in_4));  // open: en
  Register #(.trigger("falling")) register_22 (
    .D(shift_register_1_q21), .Q(out_26), .clk(in_3), .clr(in_4));  // open: en
  Register #(.trigger("falling")) register_23 (
    .D(shift_register_1_q22), .Q(out_27), .clk(in_3), .clr(in_4));  // open: en
  Register #(.trigger("falling")) register_24 (
    .D(shift_register_1_q23), .Q(out_28), .clk(in_3), .clr(in_4));  // open: en
  Register #(.trigger("falling")) register_25 (
    .D(shift_register_1_q24), .Q(out_29), .clk(in_3), .clr(in_4));  // open: en
  Register #(.trigger("falling")) register_26 (
    .D(shift_register_1_q25), .Q(out_30), .clk(in_3), .clr(in_4));  // open: en
  Register #(.trigger("falling")) register_27 (
    .D(shift_register_1_q26), .Q(out_31), .clk(in_3), .clr(in_4));  // open: en
  Register #(.trigger("falling")) register_28 (
    .D(shift_register_1_q27), .Q(out_32), .clk(in_3), .clr(in_4));  // open: en
  Register #(.trigger("falling")) register_29 (
    .D(shift_register_1_q28), .Q(out_33), .clk(in_3), .clr(in_4));  // open: en
  Register #(.trigger("falling")) register_30 (
    .D(shift_register_1_q29), .Q(out_34), .clk(in_3), .clr(in_4));  // open: en
  Register #(.trigger("falling")) register_31 (
    .D(shift_register_1_q30), .Q(out_35), .clk(in_3), .clr(in_4));  // open: en
  Register #(.trigger("falling")) register_32 (
    .D(shift_register_1_q31), .Q(out_36), .clk(in_3), .clr(in_4));  // open: en
  DotMatrix #(.matrixcols(32), .matrixrows(8)) dotmatrix_1 (
    .col0(out_5), .col1(out_6), .col2(out_7), .col3(out_8), .col4(out_9), .col5(out_10), .col6(out_11),
    .col7(out_12), .col8(out_13), .col9(out_14), .col10(out_15), .col11(out_16), .col12(out_17),
    .col13(out_18), .col14(out_19), .col15(out_20), .col16(out_21), .col17(out_22), .col18(out_23),
    .col19(out_24), .col20(out_25), .col21(out_26), .col22(out_27), .col23(out_28), .col24(out_29),
    .col25(out_30), .col26(out_31), .col27(out_32), .col28(out_33), .col29(out_34), .col30(out_35),
    .col31(out_36));
endmodule

module stack_pointer (
  input  in_1,
  input  sp_sel,
  input  in_3,
  input  in_4,
  output [7:0] out_5
);

  wire and_1_out, and_2_out, and_3_out, multiplexer_1_out, multiplexer_2_out, or_1_out;

  and and_1 (and_1_out, ~in_1, sp_sel);  // AND_Gate
  and and_2 (and_2_out, ~in_1, sp_sel);  // AND_Gate
  and and_3 (and_3_out, in_1, sp_sel);
  or or_1 (or_1_out, and_2_out, and_3_out);
  Multiplexer #(.enable("false")) multiplexer_1 (.in0(and_1_out), .in1(1'b1), .out(multiplexer_1_out), .sel(in_4));
  Multiplexer #(.enable("false")) multiplexer_2 (.in0(or_1_out), .in1(1'b0), .out(multiplexer_2_out), .sel(in_4));
  Counter #(.trigger("falling")) counter_1 (
    .load(multiplexer_1_out), .D({8{1'b1}}), .count(multiplexer_2_out), .Q(out_5), .clk(in_3));  // open: carry, clr

  // Notes on the sheet:
  //   sp++/sp--
endmodule
